# Fritzing sketch BreadboardCircuit (saved by Fritzing 0.9.3b)
breadboards: 1

parts:
  Part1 = Arduino Uno (Rev3)
  J1 = Basic Servo
  Part2 = Bluetooth HC-05 Macho
  U1 = LIPO-1000mAh [package=lipo-1000]
  R4 = Resistor [tolerance=±5% resistance=100k package=THT]
  R2 = Resistor [tolerance=±5% resistance=10k package=THT]
  R3 = Resistor [tolerance=±5% resistance=10k package=THT]

nets:
  N1: Part1.A0, J1.pulse
  N2: Part1.A1, R4.Pin_0, R2.Pin_0
  N3: Part1.D8, Part2.TXD
  N4: Part1.D9_PWM, Part2.RXD
  VCC: Part1.5V, J1.vcc, Part2.VCC
  GND: Part1.GND, J1.gnd, Part2.GND, U1.-, R3.Pin_1
  N5: U1.+, R4.Pin_1
  N6: R2.Pin_1, R3.Pin_0
